// Logisim project Intellegent 404.circ as structural Verilog: 2 circuits, main circuit CPU
module ALU (
  input  [3:0] Instruction,
  input  [7:0] in_2,
  input  [7:0] in_3,
  output [7:0] out_4,
  output [7:0] out_5,
  output Flag_C_B,
  output Flag_Z
);

  wire adder_1_cout, adder_2_cout, decoder_1_out0, decoder_1_out1, decoder_1_out2, decoder_1_out3,
       decoder_1_out4, decoder_1_out5, decoder_1_out6, decoder_1_out7, decoder_1_out8, decoder_1_out9,
       decoder_1_out10, decoder_1_out11, decoder_1_out12, decoder_1_out13, decoder_1_out14, decoder_1_out15,
       subtractor_1_bout, subtractor_2_bout;
  wire [7:0] adder_1_out, adder_2_out, and_1_out, controlled_buffer_1_out, controlled_buffer_2_out,
       controlled_buffer_4_out, controlled_buffer_6_out, controlled_buffer_7_out, controlled_buffer_10_out,
       controlled_buffer_12_out, controlled_buffer_14_out, controlled_buffer_18_out,
       controlled_buffer_19_out, controlled_buffer_22_out, controlled_buffer_23_out,
       controlled_buffer_26_out, controlled_buffer_28_out, controlled_buffer_30_out,
       controlled_buffer_33_out, controlled_buffer_37_out, controlled_buffer_38_out,
       controlled_buffer_42_out, controlled_buffer_43_out, controlled_buffer_46_out,
       controlled_buffer_47_out, controlled_buffer_48_out, controlled_buffer_51_out,
       controlled_buffer_53_out, controlled_buffer_55_out, divider_1_out, divider_1_rem, multiplier_1_cout,
       multiplier_1_out, nand_1_out, nor_1_out, or_1_out, shifter_1_out, shifter_2_out, subtractor_1_out,
       subtractor_2_out, xnor_1_out, xor_1_out;

  Decoder #(.select(4)) decoder_1 (
    .out0(decoder_1_out0), .out1(decoder_1_out1), .out2(decoder_1_out2), .out3(decoder_1_out3),
    .out4(decoder_1_out4), .out5(decoder_1_out5), .out6(decoder_1_out6), .out7(decoder_1_out7),
    .out8(decoder_1_out8), .out9(decoder_1_out9), .out10(decoder_1_out10), .out11(decoder_1_out11),
    .out12(decoder_1_out12), .out13(decoder_1_out13), .out14(decoder_1_out14), .out15(decoder_1_out15),
    .sel(Instruction));  // open: en
  Comparator comparator_1 (.a(out_4), .b({8{1'b0}}), .eq(Flag_Z));  // open: gt, lt
  assign controlled_buffer_1_out = decoder_1_out1 ? in_2 : 8'bz;  // Controlled_Buffer controlled_buffer_1
  assign controlled_buffer_2_out = decoder_1_out1 ? in_3 : 8'bz;  // Controlled_Buffer controlled_buffer_2
  assign Flag_C_B = decoder_1_out1 ? adder_1_cout : 1'bz;  // Controlled_Buffer controlled_buffer_3
  assign controlled_buffer_4_out = decoder_1_out2 ? in_2 : 8'bz;  // Controlled_Buffer controlled_buffer_4
  Adder adder_1 (
    .a(controlled_buffer_1_out), .b(controlled_buffer_2_out), .out(adder_1_out), .cout(adder_1_cout));  // open: cin
  assign out_4 = decoder_1_out1 ? adder_1_out : 8'bz;  // Controlled_Buffer controlled_buffer_5
  assign controlled_buffer_6_out = decoder_1_out2 ? in_3 : 8'bz;  // Controlled_Buffer controlled_buffer_6
  assign controlled_buffer_7_out = decoder_1_out3 ? in_2 : 8'bz;  // Controlled_Buffer controlled_buffer_7
  Subtractor subtractor_1 (
    .a(controlled_buffer_4_out), .b(controlled_buffer_6_out), .out(subtractor_1_out), .bout(subtractor_1_bout));  // open: bin
  assign out_4 = decoder_1_out2 ? subtractor_1_out : 8'bz;  // Controlled_Buffer controlled_buffer_8
  assign Flag_C_B = decoder_1_out2 ? subtractor_1_bout : 1'bz;  // Controlled_Buffer controlled_buffer_9
  assign and_1_out = controlled_buffer_7_out & controlled_buffer_10_out;  // AND_Gate and_1, 8 bits wide
  assign controlled_buffer_10_out = decoder_1_out3 ? in_3 : 8'bz;  // Controlled_Buffer controlled_buffer_10
  assign Flag_C_B = decoder_1_out3 ? 1'b0 : 1'bz;  // Controlled_Buffer controlled_buffer_11
  assign controlled_buffer_12_out = decoder_1_out4 ? in_2 : 8'bz;  // Controlled_Buffer controlled_buffer_12
  assign out_4 = decoder_1_out3 ? and_1_out : 8'bz;  // Controlled_Buffer controlled_buffer_13
  assign or_1_out = controlled_buffer_12_out | controlled_buffer_14_out;  // OR_Gate or_1, 8 bits wide
  assign controlled_buffer_14_out = decoder_1_out4 ? in_3 : 8'bz;  // Controlled_Buffer controlled_buffer_14
  assign out_4 = decoder_1_out4 ? or_1_out : 8'bz;  // Controlled_Buffer controlled_buffer_15
  assign Flag_C_B = decoder_1_out4 ? 1'b0 : 1'bz;  // Controlled_Buffer controlled_buffer_16
  assign out_4 = decoder_1_out5 ? ~in_2 : 8'bz;  // Controlled_Inverter controlled_inverter_1
  assign Flag_C_B = decoder_1_out5 ? 1'b0 : 1'bz;  // Controlled_Buffer controlled_buffer_17
  assign controlled_buffer_18_out = decoder_1_out6 ? in_2 : 8'bz;  // Controlled_Buffer controlled_buffer_18
  assign controlled_buffer_19_out = decoder_1_out6 ? in_3 : 8'bz;  // Controlled_Buffer controlled_buffer_19
  Shifter shifter_1 (.in(controlled_buffer_18_out), .\dist (controlled_buffer_19_out[2:0]), .out(shifter_1_out));
  assign out_4 = decoder_1_out6 ? shifter_1_out : 8'bz;  // Controlled_Buffer controlled_buffer_20
  assign Flag_C_B = decoder_1_out6 ? 1'b0 : 1'bz;  // Controlled_Buffer controlled_buffer_21
  assign controlled_buffer_22_out = decoder_1_out7 ? in_2 : 8'bz;  // Controlled_Buffer controlled_buffer_22
  assign controlled_buffer_23_out = decoder_1_out7 ? in_3 : 8'bz;  // Controlled_Buffer controlled_buffer_23
  Shifter #(.shift("lr")) shifter_2 (
    .in(controlled_buffer_22_out), .\dist (controlled_buffer_23_out[2:0]), .out(shifter_2_out));
  assign Flag_C_B = decoder_1_out7 ? 1'b0 : 1'bz;  // Controlled_Buffer controlled_buffer_24
  assign out_4 = decoder_1_out7 ? shifter_2_out : 8'bz;  // Controlled_Buffer controlled_buffer_25
  assign controlled_buffer_26_out = decoder_1_out8 ? in_2 : 8'bz;  // Controlled_Buffer controlled_buffer_26
  assign Flag_C_B = decoder_1_out8 ? adder_2_cout : 1'bz;  // Controlled_Buffer controlled_buffer_27
  assign controlled_buffer_28_out = decoder_1_out9 ? in_2 : 8'bz;  // Controlled_Buffer controlled_buffer_28
  Adder adder_2 (.a(controlled_buffer_26_out), .b(8'h1), .out(adder_2_out), .cout(adder_2_cout));  // open: cin
  assign out_4 = decoder_1_out8 ? adder_2_out : 8'bz;  // Controlled_Buffer controlled_buffer_29
  assign controlled_buffer_30_out = decoder_1_out10 ? in_2 : 8'bz;  // Controlled_Buffer controlled_buffer_30
  Subtractor subtractor_2 (
    .a(controlled_buffer_28_out), .b(8'h1), .out(subtractor_2_out), .bout(subtractor_2_bout));  // open: bin
  assign out_4 = decoder_1_out9 ? subtractor_2_out : 8'bz;  // Controlled_Buffer controlled_buffer_31
  assign Flag_C_B = decoder_1_out9 ? subtractor_2_bout : 1'bz;  // Controlled_Buffer controlled_buffer_32
  assign controlled_buffer_33_out = decoder_1_out10 ? in_3 : 8'bz;  // Controlled_Buffer controlled_buffer_33
  assign Flag_C_B = decoder_1_out10 ? 1'b0 : 1'bz;  // Controlled_Buffer controlled_buffer_34
  Multiplier multiplier_1 (
    .a(controlled_buffer_30_out), .b(controlled_buffer_33_out), .out(multiplier_1_out),
    .cout(multiplier_1_cout));  // open: cin
  assign out_4 = decoder_1_out10 ? multiplier_1_out : 8'bz;  // Controlled_Buffer controlled_buffer_35
  assign out_5 = decoder_1_out10 ? multiplier_1_cout : 8'bz;  // Controlled_Buffer controlled_buffer_36
  assign controlled_buffer_37_out = decoder_1_out11 ? in_2 : 8'bz;  // Controlled_Buffer controlled_buffer_37
  assign controlled_buffer_38_out = decoder_1_out11 ? in_3 : 8'bz;  // Controlled_Buffer controlled_buffer_38
  Divider divider_1 (
    .a(controlled_buffer_37_out), .b(controlled_buffer_38_out), .out(divider_1_out), .rem(divider_1_rem));  // open: upper
  assign out_5 = decoder_1_out11 ? divider_1_rem : 8'bz;  // Controlled_Buffer controlled_buffer_39
  assign out_4 = decoder_1_out11 ? divider_1_out : 8'bz;  // Controlled_Buffer controlled_buffer_40
  assign Flag_C_B = decoder_1_out11 ? 1'b0 : 1'bz;  // Controlled_Buffer controlled_buffer_41
  assign controlled_buffer_42_out = decoder_1_out12 ? in_2 : 8'bz;  // Controlled_Buffer controlled_buffer_42
  assign controlled_buffer_43_out = decoder_1_out12 ? in_3 : 8'bz;  // Controlled_Buffer controlled_buffer_43
  assign nand_1_out = ~(controlled_buffer_42_out & controlled_buffer_43_out);  // NAND_Gate nand_1, 8 bits wide
  assign Flag_C_B = decoder_1_out12 ? 1'b0 : 1'bz;  // Controlled_Buffer controlled_buffer_44
  assign out_4 = decoder_1_out12 ? nand_1_out : 8'bz;  // Controlled_Buffer controlled_buffer_45
  assign controlled_buffer_46_out = decoder_1_out13 ? in_2 : 8'bz;  // Controlled_Buffer controlled_buffer_46
  assign controlled_buffer_47_out = decoder_1_out13 ? in_3 : 8'bz;  // Controlled_Buffer controlled_buffer_47
  assign controlled_buffer_48_out = decoder_1_out14 ? in_2 : 8'bz;  // Controlled_Buffer controlled_buffer_48
  assign nor_1_out = ~(controlled_buffer_46_out | controlled_buffer_47_out);  // NOR_Gate nor_1, 8 bits wide
  assign out_4 = decoder_1_out13 ? nor_1_out : 8'bz;  // Controlled_Buffer controlled_buffer_49
  assign Flag_C_B = decoder_1_out13 ? 1'b0 : 1'bz;  // Controlled_Buffer controlled_buffer_50
  assign controlled_buffer_51_out = decoder_1_out14 ? in_3 : 8'bz;  // Controlled_Buffer controlled_buffer_51
  assign Flag_C_B = decoder_1_out14 ? 1'b0 : 1'bz;  // Controlled_Buffer controlled_buffer_52
  assign controlled_buffer_53_out = decoder_1_out15 ? in_2 : 8'bz;  // Controlled_Buffer controlled_buffer_53
  assign xor_1_out = controlled_buffer_48_out ^ controlled_buffer_51_out;  // XOR_Gate xor_1, 8 bits wide
  assign out_4 = decoder_1_out14 ? xor_1_out : 8'bz;  // Controlled_Buffer controlled_buffer_54
  assign controlled_buffer_55_out = decoder_1_out15 ? in_3 : 8'bz;  // Controlled_Buffer controlled_buffer_55
  assign Flag_C_B = decoder_1_out15 ? 1'b0 : 1'bz;  // Controlled_Buffer controlled_buffer_56
  assign xnor_1_out = ~(controlled_buffer_53_out ^ controlled_buffer_55_out);  // XNOR_Gate xnor_1, 8 bits wide
  assign out_4 = decoder_1_out15 ? xnor_1_out : 8'bz;  // Controlled_Buffer controlled_buffer_57

  // Notes on the sheet:
  //   INPUT 1
  //   INPUT 2
  //   OUTPUT
  //   OUTPUT OTHER
  //   A
  //   B
  //   C
  //   C_OUT
  //   NOP
  //   NOP
  //   ADD
  //   SUB
  //   AND
  //   0000
  //   0001
  //   0010
  //   0011
  //   ADD
  //   C - carry
  //   ALU
  //   0100
  //   OR
  //   NOT
  //   0101
  //   0110
  //   SL
  //   0111
  //   SR
  //   INC
  //   DEC
  //   MUL
  //   DIV
  //   SUB
  //   B - negative
  //   1000
  //   1001
  //   1010
  //   1011
  //   1100
  //   NAND
  //   NOR
  //   1101
  //   1110
  //   XOR
  //   XNOR
  //   1111
  //   AND
  //   OR
  //   NOT
  //   SL
  //   SR
  //   INC
  //   C - carry
  //   DEC
  //   B - negative
  //   MUL
  //   DIV
  //   NAND
  //   NOR
  //   XOR
  //   XNOR
endmodule

module CPU (
);

  wire ACC_INPUT, ACC_OUTPUT, ALU_INPUT, ALU_OUT_EXTRA, ALU_OUT_FLAGS, ALU_OUT_RESULT, ALU_RESULT,
       ALU_TEMP_INPUT, and_1_out, and_2_out, and_3_out, and_4_out, and_5_out, and_6_out, and_7_out,
       and_8_out, and_9_out, and_10_out, and_11_out, and_12_out, and_13_out, and_14_out, B__INPUT, B_OUTPUT,
       clock_1_out, decoder_1_out1, decoder_1_out2, decoder_1_out3, decoder_1_out4, decoder_1_out5,
       decoder_1_out6, decoder_1_out7, F__INPUT, F_OUTPUT, IR__INPUT, IR_OUTPUT, not_1_out, not_2_out,
       not_3_out, not_4_out, OPP_INPUT, OPP_RESET, PC__INPUT, PC_OUTPUT, PROG_ADDRESS, PROG_OUTPUT,
       RAM_ADDRESS, RAM_INPUT, RAM_OUTPUT, REG_ADDRESS_E, REG_ADDRESS_INPUT, REG_I_O;
  wire [1:0] alu_1_flag_c_b;
  wire [2:0] controlled_buffer_17_out;
  wire [3:0] ALU_INSTRUCTION;
  wire [7:0] A_q, alu_1_out_4, alu_1_out_5, ALU_INPUT_q, ALU_OUT_EXTRA_q, ALU_OUT_FLAGS_q, ALU_OUT_RES_q,
       B_q, controlled_buffer_1_out, controlled_buffer_2_out, controlled_buffer_3_out,
       controlled_buffer_4_out, controlled_buffer_7_out, controlled_buffer_8_out, controlled_buffer_11_out,
       controlled_buffer_12_out, controlled_buffer_16_out, controlled_buffer_19_out,
       controlled_buffer_20_out, controlled_buffer_21_out, controlled_buffer_24_out,
       controlled_buffer_26_out, controlled_buffer_27_out, controlled_buffer_30_out,
       controlled_buffer_31_out, controlled_buffer_34_out, controlled_buffer_36_out,
       controlled_buffer_37_out, FLAG_q, IR_q, PC_q, PROG_ADDRESS_TEMP_q, R0_q, R1_q, R2_q, R3_q, R4_q, R5_q,
       R6_q, ram_1_data, RAM_ADDRESS_TEMP_q, REG_ADDRESS_q, rom_2_data;
  wire [7:3] controlled_buffer_18_out;
  wire [11:0] OPCODE_q;
  wire [31:12] rom_1_data;

  Clock clock_1 (.out(clock_1_out));
  Register A (.D(controlled_buffer_1_out), .en(ACC_INPUT), .Q(A_q), .clk(clock_1_out));  // open: clr
  assign controlled_buffer_1_out = ACC_INPUT ? controlled_buffer_2_out : 8'bz;  // Controlled_Buffer controlled_buffer_1
  assign controlled_buffer_2_out = ACC_OUTPUT ? A_q : 8'bz;  // Controlled_Buffer controlled_buffer_2
  assign controlled_buffer_3_out = B__INPUT ? controlled_buffer_2_out : 8'bz;  // Controlled_Buffer controlled_buffer_3
  Register B (.D(controlled_buffer_3_out), .en(B__INPUT), .Q(B_q), .clk(clock_1_out));  // open: clr
  assign controlled_buffer_4_out = PC__INPUT ? controlled_buffer_2_out : 8'bz;  // Controlled_Buffer controlled_buffer_4
  assign controlled_buffer_2_out = B_OUTPUT ? B_q : 8'bz;  // Controlled_Buffer controlled_buffer_5
  Register PC (.D(controlled_buffer_4_out), .en(PC__INPUT), .Q(PC_q), .clk(clock_1_out));  // open: clr
  assign controlled_buffer_2_out = PC_OUTPUT ? PC_q : 8'bz;  // Controlled_Buffer controlled_buffer_6
  Register IR (.D(controlled_buffer_7_out), .en(IR__INPUT), .Q(IR_q), .clk(clock_1_out));  // open: clr
  assign controlled_buffer_7_out = IR__INPUT ? controlled_buffer_2_out : 8'bz;  // Controlled_Buffer controlled_buffer_7
  assign controlled_buffer_8_out = F__INPUT ? controlled_buffer_2_out : 8'bz;  // Controlled_Buffer controlled_buffer_8
  assign controlled_buffer_2_out = IR_OUTPUT ? IR_q : 8'bz;  // Controlled_Buffer controlled_buffer_9
  Register FLAG (.D(controlled_buffer_8_out), .en(F__INPUT), .Q(FLAG_q), .clk(clock_1_out));  // open: clr
  assign controlled_buffer_2_out = F_OUTPUT ? FLAG_q : 8'bz;  // Controlled_Buffer controlled_buffer_10
  assign controlled_buffer_11_out = ALU_TEMP_INPUT ? controlled_buffer_2_out : 8'bz;  // Controlled_Buffer controlled_buffer_11
  Register u_ALU_INPUT (
    .D(controlled_buffer_11_out), .en(ALU_TEMP_INPUT), .Q(ALU_INPUT_q), .clk(clock_1_out));  // open: clr
  assign controlled_buffer_12_out = ALU_INPUT ? controlled_buffer_2_out : 8'bz;  // Controlled_Buffer controlled_buffer_12
  ALU alu_1 (
    .Instruction(ALU_INSTRUCTION), .in_2(controlled_buffer_12_out), .in_3(ALU_INPUT_q), .out_4(alu_1_out_4),
    .out_5(alu_1_out_5), .Flag_C_B(alu_1_flag_c_b[0]), .Flag_Z(alu_1_flag_c_b[1]));
  Register ALU_OUT_RES (.D(alu_1_out_4), .en(ALU_RESULT), .Q(ALU_OUT_RES_q), .clk(clock_1_out));  // open: clr
  Register u_ALU_OUT_EXTRA (.D(alu_1_out_5), .en(ALU_RESULT), .Q(ALU_OUT_EXTRA_q), .clk(clock_1_out));  // open: clr
  Register u_ALU_OUT_FLAGS (
    .D({{6{1'b0}}, alu_1_flag_c_b}), .en(ALU_RESULT), .Q(ALU_OUT_FLAGS_q), .clk(clock_1_out));  // open: clr
  assign controlled_buffer_2_out = ALU_OUT_FLAGS ? ALU_OUT_FLAGS_q : 8'bz;  // Controlled_Buffer controlled_buffer_13
  assign controlled_buffer_2_out = ALU_OUT_EXTRA ? ALU_OUT_EXTRA_q : 8'bz;  // Controlled_Buffer controlled_buffer_14
  assign controlled_buffer_2_out = ALU_OUT_RESULT ? ALU_OUT_RES_q : 8'bz;  // Controlled_Buffer controlled_buffer_15
  assign controlled_buffer_16_out = REG_ADDRESS_INPUT ? controlled_buffer_2_out : 8'bz;  // Controlled_Buffer controlled_buffer_16
  assign controlled_buffer_17_out = not_1_out ? 3'b000 : 3'bz;  // Controlled_Buffer controlled_buffer_17
  not not_1 (not_1_out, REG_ADDRESS_E);
  assign {controlled_buffer_18_out, controlled_buffer_17_out} = REG_ADDRESS_E ? REG_ADDRESS_q : 8'bz;  // Controlled_Buffer controlled_buffer_18
  Register REG_ADDRESS (.D(controlled_buffer_16_out), .Q(REG_ADDRESS_q), .clk(clock_1_out));  // open: en, clr
  not not_2 (not_2_out, clock_1_out);
  Decoder #(.select(3)) decoder_1 (
    .out1(decoder_1_out1), .out2(decoder_1_out2), .out3(decoder_1_out3), .out4(decoder_1_out4),
    .out5(decoder_1_out5), .out6(decoder_1_out6), .out7(decoder_1_out7), .sel(controlled_buffer_17_out));  // open: out0, en
  not not_3 (not_3_out, REG_I_O);
  assign controlled_buffer_19_out = OPP_INPUT ? controlled_buffer_2_out : 8'bz;  // Controlled_Buffer controlled_buffer_19
  and and_1 (and_1_out, REG_I_O, decoder_1_out7);
  Register R6 (.D(controlled_buffer_20_out), .en(and_1_out), .Q(R6_q), .clk(clock_1_out));  // open: clr
  assign controlled_buffer_20_out = and_1_out ? controlled_buffer_2_out : 8'bz;  // Controlled_Buffer controlled_buffer_20
  Counter #(.width(12), .max('hfff)) OPCODE (
    .load(OPP_INPUT), .D({controlled_buffer_19_out, 4'b0000}), .count(not_4_out), .Q(OPCODE_q),
    .clk(not_2_out), .clr(OPP_RESET));  // open: carry
  not not_4 (not_4_out, OPP_INPUT);
  and and_2 (and_2_out, REG_I_O, decoder_1_out6);
  and and_3 (and_3_out, not_3_out, decoder_1_out7);
  assign controlled_buffer_21_out = and_2_out ? controlled_buffer_2_out : 8'bz;  // Controlled_Buffer controlled_buffer_21
  assign controlled_buffer_2_out = and_3_out ? R6_q : 8'bz;  // Controlled_Buffer controlled_buffer_22
  and and_4 (and_4_out, not_3_out, decoder_1_out6);
  Register R5 (.D(controlled_buffer_21_out), .en(and_2_out), .Q(R5_q), .clk(clock_1_out));  // open: clr
  assign controlled_buffer_2_out = and_4_out ? R5_q : 8'bz;  // Controlled_Buffer controlled_buffer_23
  ROM #(.addrWidth(12), .dataWidth(32)) rom_1 (
    .addr(OPCODE_q),
    .data({rom_1_data[31], OPP_RESET, OPP_INPUT, RAM_OUTPUT, RAM_INPUT, RAM_ADDRESS, PROG_OUTPUT, PROG_ADDRESS, ALU_OUT_FLAGS, ALU_OUT_EXTRA, ALU_OUT_RESULT, ALU_RESULT, ALU_INPUT, ALU_TEMP_INPUT, ALU_INSTRUCTION, REG_I_O, rom_1_data[12], REG_ADDRESS_INPUT, REG_ADDRESS_E, F_OUTPUT, F__INPUT, IR_OUTPUT, IR__INPUT, PC_OUTPUT, PC__INPUT, B_OUTPUT, B__INPUT, ACC_OUTPUT, ACC_INPUT}));  // open: sel
  and and_5 (and_5_out, REG_I_O, decoder_1_out5);
  and and_6 (and_6_out, not_3_out, decoder_1_out5);
  Register R4 (.D(controlled_buffer_24_out), .en(and_5_out), .Q(R4_q), .clk(clock_1_out));  // open: clr
  assign controlled_buffer_24_out = and_5_out ? controlled_buffer_2_out : 8'bz;  // Controlled_Buffer controlled_buffer_24
  assign controlled_buffer_2_out = and_6_out ? R4_q : 8'bz;  // Controlled_Buffer controlled_buffer_25
  and and_7 (and_7_out, REG_I_O, decoder_1_out4);
  assign controlled_buffer_26_out = and_7_out ? controlled_buffer_2_out : 8'bz;  // Controlled_Buffer controlled_buffer_26
  and and_8 (and_8_out, REG_I_O, decoder_1_out3);
  and and_9 (and_9_out, not_3_out, decoder_1_out4);
  Register R3 (.D(controlled_buffer_26_out), .en(and_7_out), .Q(R3_q), .clk(clock_1_out));  // open: clr
  assign controlled_buffer_27_out = and_8_out ? controlled_buffer_2_out : 8'bz;  // Controlled_Buffer controlled_buffer_27
  assign controlled_buffer_2_out = and_9_out ? R3_q : 8'bz;  // Controlled_Buffer controlled_buffer_28
  and and_10 (and_10_out, not_3_out, decoder_1_out3);
  Register R2 (.D(controlled_buffer_27_out), .en(and_8_out), .Q(R2_q), .clk(clock_1_out));  // open: clr
  assign controlled_buffer_2_out = and_10_out ? R2_q : 8'bz;  // Controlled_Buffer controlled_buffer_29
  and and_11 (and_11_out, not_3_out, decoder_1_out2);
  and and_12 (and_12_out, REG_I_O, decoder_1_out2);
  Register R1 (.D(controlled_buffer_30_out), .en(and_12_out), .Q(R1_q), .clk(clock_1_out));  // open: clr
  assign controlled_buffer_30_out = and_12_out ? controlled_buffer_2_out : 8'bz;  // Controlled_Buffer controlled_buffer_30
  and and_13 (and_13_out, REG_I_O, decoder_1_out1);
  assign controlled_buffer_31_out = and_13_out ? controlled_buffer_2_out : 8'bz;  // Controlled_Buffer controlled_buffer_31
  assign controlled_buffer_2_out = and_11_out ? R1_q : 8'bz;  // Controlled_Buffer controlled_buffer_32
  and and_14 (and_14_out, not_3_out, decoder_1_out1);
  Register R0 (.D(controlled_buffer_31_out), .en(and_13_out), .Q(R0_q), .clk(clock_1_out));  // open: clr
  assign controlled_buffer_2_out = and_14_out ? R0_q : 8'bz;  // Controlled_Buffer controlled_buffer_33
  assign controlled_buffer_34_out = PROG_ADDRESS ? controlled_buffer_2_out : 8'bz;  // Controlled_Buffer controlled_buffer_34
  Register PROG_ADDRESS_TEMP (
    .D(controlled_buffer_34_out), .en(PROG_ADDRESS), .Q(PROG_ADDRESS_TEMP_q), .clk(clock_1_out));  // open: clr
  ROM rom_2 (.addr(PROG_ADDRESS_TEMP_q), .data(rom_2_data), .sel(PROG_OUTPUT));
  assign controlled_buffer_2_out = PROG_OUTPUT ? rom_2_data : 8'bz;  // Controlled_Buffer controlled_buffer_35
  Register RAM_ADDRESS_TEMP (
    .D(controlled_buffer_36_out), .en(RAM_ADDRESS), .Q(RAM_ADDRESS_TEMP_q), .clk(clock_1_out));  // open: clr
  assign controlled_buffer_36_out = RAM_ADDRESS ? controlled_buffer_2_out : 8'bz;  // Controlled_Buffer controlled_buffer_36
  assign controlled_buffer_37_out = RAM_INPUT ? controlled_buffer_2_out : 8'bz;  // Controlled_Buffer controlled_buffer_37
  RAM #(.bus("separate")) ram_1 (
    .addr(RAM_ADDRESS_TEMP_q), .din(controlled_buffer_37_out), .data(ram_1_data), .str(RAM_INPUT),
    .clk(clock_1_out), .ld(RAM_OUTPUT));  // open: sel, clr
  assign controlled_buffer_2_out = RAM_OUTPUT ? ram_1_data : 8'bz;  // Controlled_Buffer controlled_buffer_38

  // Notes on the sheet:
  //   Main Bus
  //   Clock Pulse
  //   Flags 01 C
  //   Flags 02 Z
  //   Flags 03 C and Z
  //   Main Bus
  //   Main Bus
  //   MICRO OPERATIONS
  //   contents of rom_1 (hex, n*v repeats v):
  //   1000020 2000040 20000080 13*0 1a0020 1200010 2000001 11a0020 200010 40000000 10*0 1a0020 1200010
  //   2000004 11a0020 200010 40000000 10*0 1a0020 1200010 2000001 1a0020 1200010 2000004 802 2408 1a0020
  //   1200010 40000000 5*0 1a0020 1200010 2000004 808 401 1a0020 1200010 40000000 8*0 1a0020 1200010
  //   2000004 808 2402 1a0020 1200010 40000000 8*0 9 1a0020 1200010 40000000 12*0 6 1a0020 1200010
  //   40000000 12*0 1a0020 1200010 2000004 4000008 8000002 1a0020 1200010 40000000 8*0 1a0020 1200010
  //   2000004 4000008 10000001 1a0020 1200010 40000000 8*0 1a0020 1200010 2000001 1a0020 1200010 2000004
  //   4000002 8000008 1a0020 1200010 40000000 5*0 40008 184002 200001 800100 1a0020 1200010 40000000 9*0
  //   40008 188002 200001 800100 1a0020 1200010 40000000 9*0 40008 18c002 200001 800100 1a0020 1200010
  //   40000000 9*0 40008 190002 200001 800100 1a0020 1200010 40000000 9*0 194002 200001 800100 1a0020
  //   1200010 40000000 10*0 40008 198002 200001 800100 1a0020 1200010 40000000 9*0 40008 19c002 200001
  //   800100 1a0020 1200010 40000000 9*0 1a0002 200001 800100 1a0020 1200010 40000000 10*0 1a4002 200001
  //   800100 1a0020 1200010 40000000 10*0 40008 1a8002 200001 400004 800100 1a0020 1200010 40000000 8*0
  //   40008 1ac002 200001 400004 800100 1a0020 1200010 40000000 8*0 40008 1b0002 200001 800100 1a0020
  //   1200010 40000000 9*0 40008 1b4002 200001 800100 1a0020 1200010 40000000 9*0 40008 1b8002 200001
  //   800100 1a0020 1200010 40000000 9*0 40008 1bc002 200001 800100 1a0020 1200010 40000000 9*0 1a0020
  //   1200010 2000001 1000012 40000000
  //   Control Signals
  //   Main Bus
  //   CODE MEMORY
  //   PROGRAM
  //   Main Bus
  //   RAM MEMORY
  //   RAM MEMORY
  //   Main Bus
endmodule
